# Fritzing sketch wiring-diagram (saved by Fritzing 0.9.3b)

parts:
  LED2 = LED - 5mm [color="White (4500K)" package="5 mm [THT]"]
  R1 = Resistor [tolerance=±5% resistance=220 package="1206 [SMD]"]
  USBTTL1 = USB TTL Serial Cable

nets:
  N1: LED2.anode, USBTTL1.5V
  N2: R1.Pin_1, USBTTL1.GND
